// Logisim project Conte-200.circ as structural Verilog: 5 circuits, main circuit Datapath
module Datapath (
  output [3:0] out_1,
  output [3:0] out_2,
  output [3:0] out_3,
  output [3:0] out_4
);

  wire ALUHi, ALULo, clk, CmpOut, DrADDR, DrALU, DrMEM, DrOFF, DrPC, DrREG, LdA, LdB, LdCmp, LdIR, LdMAR,
       LdPC, rst, WrMEM, WrREG;
  wire [1:0] RegSel;
  wire [3:0] regno;
  wire [19:4] IR;
  wire [31:0] A, alu_1_output, B, bit_extender_1_out, bit_extender_2_out, DrPC_out, MAR, PC_q, ram_1_data,
       registers_1_output;

  Clock clock_1 (.out(clk));
  Button button_1 (.out(rst));
  Register #(.width(32)) PC (.D(DrPC_out), .en(LdPC), .Q(PC_q), .clk(clk), .clr(rst));
  assign DrPC_out = DrPC ? PC_q : 32'bz;  // Controlled_Buffer DrPC
  Comparison comparison_1 (.INPUT(DrPC_out), .CmpSel(out_2), .LdCmp(LdCmp), .clk(clk), .rst(rst), .CmpOut(CmpOut));
  Register #(.width(32)) register_1 (.D(DrPC_out), .en(LdA), .Q(A), .clk(clk), .clr(rst));
  ALU alu_1 (.a(A), .b(B), .\output (alu_1_output), .func({ALUHi, ALULo}));
  assign DrPC_out = DrALU ? alu_1_output : 32'bz;  // Controlled_Buffer DrALU
  Register #(.width(32)) register_2 (.D(DrPC_out), .en(LdB), .Q(B), .clk(clk), .clr(rst));
  Multiplexer #(.select(2), .width(4), .disabled(0), .enable("false")) multiplexer_1 (
    .in0(out_2), .in1(out_3), .in2(out_4), .in3(4'b1111), .out(regno), .sel(RegSel));
  Registers registers_1 (
    .\input (DrPC_out), .WrREG(WrREG), .clk(clk), .rst(rst), .regno(regno), .\output (registers_1_output));
  assign DrPC_out = DrREG ? registers_1_output : 32'bz;  // Controlled_Buffer DrREG
  Register #(.width(32)) u_MAR (.D(DrPC_out), .en(LdMAR), .Q(MAR), .clk(clk), .clr(rst));
  Register #(.width(32)) register_3 (
    .D(DrPC_out), .en(LdIR), .Q({out_1, out_2, out_3, IR, out_4}), .clk(clk), .clr(rst));
  assign DrPC_out = DrMEM ? ram_1_data : 32'bz;  // Controlled_Buffer DrMEM
  RAM #(.addrWidth(24), .dataWidth(32), .bus("separate")) ram_1 (
    .addr(MAR[23:0]), .din(DrPC_out), .data(ram_1_data), .str(WrMEM), .clk(clk), .clr(rst));  // open: sel, ld
  assign DrPC_out = DrOFF ? bit_extender_1_out : 32'bz;  // Controlled_Buffer DrOFF
  Microcontrol_Unit microcontrol_unit_1 (
    .DrREG(DrREG), .DrMEM(DrMEM), .DrALU(DrALU), .DrPC(DrPC), .DrOFF(DrOFF), .DrADDR(DrADDR), .LdPC(LdPC),
    .LdIR(LdIR), .LdMAR(LdMAR), .LdA(LdA), .LdB(LdB), .LdCmp(LdCmp), .WrREG(WrREG), .WrMEM(WrMEM),
    .RegSelLo(RegSel[0]), .RegSelHi(RegSel[1]), .ALULo(ALULo), .ALUHi(ALUHi), .OP(out_1), .CmpOut(CmpOut),
    .clk(clk), .rst(rst));
  assign bit_extender_1_out = {{12{IR[19]}}, {IR, out_4}};  // Bit_Extender bit_extender_1
  assign bit_extender_2_out = {{8{1'b0}}, {out_3, IR, out_4}};  // Bit_Extender bit_extender_2
  assign DrPC_out = DrADDR ? bit_extender_2_out : 32'bz;  // Controlled_Buffer DrADDR

  // Other names for the same wires on the sheet: func[1:0] = {ALUHi, ALULo};
  //   IR (some bits) = {out_1, out_2, out_3, out_4}; RZ[3:0] = out_4; RY[3:0] = out_3; CmpSel[3:0] = out_2;
  //   RX[3:0] = out_2; OP[3:0] = out_1; RegSelLo = RegSel[0]; RegSelHi = RegSel[1]
endmodule

module ALU (
  input  [31:0] a,
  input  [31:0] b,
  input  [1:0] func,
  output [31:0] \output 
);

  wire [31:0] adder_1_out, adder_2_out, nand_1_out, subtractor_1_out;

  assign nand_1_out = ~(a & b);  // NAND_Gate nand_1, 32 bits wide
  Multiplexer #(.select(2), .width(32), .disabled(0), .enable("false")) multiplexer_1 (
    .in0(adder_1_out), .in1(subtractor_1_out), .in2(nand_1_out), .in3(adder_2_out), .out(\output ), .sel(func));
  Adder #(.width(32)) adder_1 (.a(a), .b(b), .out(adder_1_out));  // open: cin, cout
  Adder #(.width(32)) adder_2 (.a(a), .b(32'h1), .out(adder_2_out));  // open: cin, cout
  Subtractor #(.width(32)) subtractor_1 (.a(a), .b(b), .out(subtractor_1_out));  // open: bin, bout
endmodule

module Registers (
  input  [31:0] \input ,
  input  WrREG,
  input  clk,
  input  rst,
  input  [3:0] regno,
  output [31:0] \output 
);

  wire Wr_a0, Wr_a1, Wr_a2, Wr_at, Wr_fp, Wr_k0, Wr_ra, Wr_s0, Wr_s1, Wr_s2, Wr_sp, Wr_t0, Wr_t1, Wr_t2,
       Wr_v0, Wr_zero;
  wire [31:0] a0, a1, a2, at, fp, k0, R_a0, R_a1, R_a2, R_at, R_fp, R_k0, R_ra, R_s0, R_s1, R_s2, R_sp, R_t0,
       R_t1, R_t2, R_v0, R_zero, ra, s0, s1, s2, sp, t0, t1, t2, v0;

  Demultiplexer #(.select(4), .width(32), .disabled(0), .enable("false")) demultiplexer_1 (
    .out1(at), .out2(v0), .out3(a0), .out4(a1), .out5(a2), .out6(t0), .out7(t1), .out8(t2), .out9(s0),
    .out10(s1), .out11(s2), .out12(k0), .out13(sp), .out14(fp), .out15(ra), .in(\input ), .sel(regno));  // open: out0
  Demultiplexer #(.select(4), .disabled(0), .enable("false")) demultiplexer_2 (
    .out0(Wr_zero), .out1(Wr_at), .out2(Wr_v0), .out3(Wr_a0), .out4(Wr_a1), .out5(Wr_a2), .out6(Wr_t0),
    .out7(Wr_t1), .out8(Wr_t2), .out9(Wr_s0), .out10(Wr_s1), .out11(Wr_s2), .out12(Wr_k0), .out13(Wr_sp),
    .out14(Wr_fp), .out15(Wr_ra), .in(WrREG), .sel(regno));
  Register #(.width(32)) register_1 (.D({32{1'b0}}), .en(Wr_zero), .Q(R_zero), .clk(clk), .clr(rst));
  Register #(.width(32)) register_2 (.D(a0), .en(Wr_a0), .Q(R_a0), .clk(clk), .clr(rst));
  Register #(.width(32)) register_3 (.D(t0), .en(Wr_t0), .Q(R_t0), .clk(clk), .clr(rst));
  Register #(.width(32)) register_4 (.D(s0), .en(Wr_s0), .Q(R_s0), .clk(clk), .clr(rst));
  Multiplexer #(.select(4), .width(32), .disabled(0), .enable("false")) multiplexer_1 (
    .in0(R_zero), .in1(R_at), .in2(R_v0), .in3(R_a0), .in4(R_a1), .in5(R_a2), .in6(R_t0), .in7(R_t1),
    .in8(R_t2), .in9(R_s0), .in10(R_s1), .in11(R_s2), .in12(R_k0), .in13(R_sp), .in14(R_fp), .in15(R_ra),
    .out(\output ), .sel(regno));
  Register #(.width(32)) register_5 (.D(at), .en(Wr_at), .Q(R_at), .clk(clk), .clr(rst));
  Register #(.width(32)) register_6 (.D(a1), .en(Wr_a1), .Q(R_a1), .clk(clk), .clr(rst));
  Register #(.width(32)) register_7 (.D(t1), .en(Wr_t1), .Q(R_t1), .clk(clk), .clr(rst));
  Register #(.width(32)) register_8 (.D(s1), .en(Wr_s1), .Q(R_s1), .clk(clk), .clr(rst));
  Register #(.width(32)) register_9 (.D(v0), .en(Wr_v0), .Q(R_v0), .clk(clk), .clr(rst));
  Register #(.width(32)) register_10 (.D(a2), .en(Wr_a2), .Q(R_a2), .clk(clk), .clr(rst));
  Register #(.width(32)) register_11 (.D(t2), .en(Wr_t2), .Q(R_t2), .clk(clk), .clr(rst));
  Register #(.width(32)) register_12 (.D(s2), .en(Wr_s2), .Q(R_s2), .clk(clk), .clr(rst));
  Register #(.width(32)) register_13 (.D(k0), .en(Wr_k0), .Q(R_k0), .clk(clk), .clr(rst));
  Register #(.width(32)) register_14 (.D(sp), .en(Wr_sp), .Q(R_sp), .clk(clk), .clr(rst));
  Register #(.width(32)) register_15 (.D(fp), .en(Wr_fp), .Q(R_fp), .clk(clk), .clr(rst));
  Register #(.width(32)) register_16 (.D(ra), .en(Wr_ra), .Q(R_ra), .clk(clk), .clr(rst));
endmodule

module Microcontrol_Unit (
  input  [3:0] OP,
  input  CmpOut,
  input  clk,
  input  rst,
  output DrREG,
  output DrMEM,
  output DrALU,
  output DrPC,
  output DrOFF,
  output DrADDR,
  output LdPC,
  output LdIR,
  output LdMAR,
  output LdA,
  output LdB,
  output LdCmp,
  output WrREG,
  output WrMEM,
  output RegSelLo,
  output RegSelHi,
  output ALULo,
  output ALUHi
);

  wire ChkCmp, OPTest;
  wire [5:0] multiplexer_1_out, rom_1_data, rom_2_data, rom_3_data, State_q;

  ROM #(.addrWidth(6), .dataWidth(26)) rom_1 (
    .addr(State_q),
    .data({ChkCmp, OPTest, ALUHi, ALULo, RegSelHi, RegSelLo, WrMEM, WrREG, LdCmp, LdB, LdA, LdMAR, LdIR, LdPC, DrADDR, DrOFF, DrPC, DrALU, DrMEM, DrREG, rom_1_data}),
    .sel(1'b1));
  Register #(.width(6)) State (.D(multiplexer_1_out), .en(1'b1), .Q(State_q), .clk(clk), .clr(rst));
  Multiplexer #(.select(2), .width(6), .disabled(0), .enable("false")) multiplexer_1 (
    .in0(rom_1_data), .in1(rom_2_data), .in2(rom_3_data), .out(multiplexer_1_out), .sel({ChkCmp, OPTest}));  // open: in3
  ROM #(.addrWidth(4), .dataWidth(6)) rom_2 (.addr(OP), .data(rom_2_data), .sel(1'b1));
  ROM #(.addrWidth(2), .dataWidth(6)) rom_3 (.addr({1'b0, CmpOut}), .data(rom_3_data), .sel(1'b1));

  // Notes on the sheet:
  //   contents of rom_1 (hex, n*v repeats v):
  //   c201 2082 c01103 1000000 208045 110046 40100 108048 10409 40100 10804b 21004c 840100 10804e 21004f
  //   420110 2008211 c01100 1800 40800 108055 10416 4117 40080 108059 1041a 411b 80040 34021d 1040 301040
  //   1f 21
  //   contents of rom_2 (hex, n*v repeats v):
  //   4 7 a d 12 13 0 0 14 18 0 0 1c 1e 0 1f
  //   contents of rom_3 (hex, n*v repeats v):
  //   0 11
endmodule

module Comparison (
  input  [31:0] INPUT,
  input  [3:0] CmpSel,
  input  LdCmp,
  input  clk,
  input  rst,
  output CmpOut
);

  wire comparator_1_eq, comparator_1_gt, multiplexer_1_out, not_1_out, not_2_out;

  Comparator #(.width(32)) comparator_1 (
    .a(INPUT), .b({32{1'b0}}), .gt(comparator_1_gt), .eq(comparator_1_eq));  // open: lt
  not not_1 (not_1_out, comparator_1_eq);
  Multiplexer #(.disabled(0), .enable("false")) multiplexer_1 (
    .in0(not_1_out), .in1(not_2_out), .out(multiplexer_1_out), .sel(CmpSel[0]));
  not not_2 (not_2_out, comparator_1_gt);
  Register #(.width(1)) CmpReg (.D(multiplexer_1_out), .en(LdCmp), .Q(CmpOut), .clk(clk), .clr(rst));
endmodule
