// Logisim project Conte-200-Pipeline.circ as structural Verilog
module main (
  input  in_1,
  output [3:0] out_2,
  output [3:0] out_3,
  output [3:0] out_4,
  output [3:0] out_5
);

  wire ADDI_out, and_1_out, CALL, CALL_out, CLK, comparator_1_eq, comparator_1_gt, Cond, E_I_type, EN, FLUSH,
       GOTO_out, LEA, LEA_out, LW_2_out, LW_out, multiplexer_11_out, not_1_out, not_2_out, not_3_out,
       or_3_out, or_5_out, register_1_q, RET_out, SKIP, SKP, STALL, SW_out, WtMem, WtReg;
  wire [3:0] DBUF_RX, DBUF_RY, DBUF_RZ, EBUF_OPCODE, EBUF_Rx, MBUF_OPCODE, MBUF_Rx, MBUF_wbrx,
       multiplexer_14_out, multiplexer_16_out, WbRx;
  wire [19:4] FBUF_IR;
  wire [23:0] bit_extender_1_out;
  wire [31:0] B_ALUout, BrPC, DBUF_A, DBUF_B, Din, E_Imm, EBUF_A, EBUF_B, EBUF_PC, FBUF_PC, FwdA, FwdB, Imm,
       INPUT, IROUT, MAR, MBUF_PC, MBUF_RESULT, multiplexer_1_out, multiplexer_2_out, multiplexer_3_out,
       multiplexer_4_out, multiplexer_6_out, multiplexer_7_out, multiplexer_12_out, multiplexer_13_out,
       multiplexer_15_out, multiplexer_17_out, multiplexer_18_out, multiplexer_19_out, NPC, Offset, PC,
       PDaddr24, ram_1_data, ram_2_data, WbPC, WbResult;

  Register #(.width(1)) register_1 (.D(1'b1), .en(and_1_out), .Q(register_1_q), .clk(CLK));  // open: clr
  and and_1 (and_1_out, out_4[3], out_4[2], out_4[1], out_4[0]);
  Clock CLOCK (.out(CLK));
  Multiplexer #(.width(32), .disabled(0), .enable("false")) multiplexer_1 (
    .in0(multiplexer_2_out), .in1(PC), .out(multiplexer_1_out), .sel(STALL));
  Register #(.width(32)) u_PC (.D(multiplexer_1_out), .en(not_1_out), .Q(PC), .clk(CLK), .clr(in_1));
  not not_1 (not_1_out, register_1_q);
  Multiplexer #(.width(32), .disabled(0), .enable("false")) multiplexer_2 (
    .in0(NPC), .in1(BrPC), .out(multiplexer_2_out), .sel(Cond));
  Bit_Extender #(.in_width(32), .out_width(24), .\type ("sign")) bit_extender_1 (.in(PC), .out(bit_extender_1_out));
  Forwarding_Unit forwarding_unit_1 (
    .SR1(out_2), .SR2(out_3), .EBUF_RESULT(B_ALUout), .MBUF_RESULT(MBUF_RESULT), .WbResult(WbResult),
    .EBUF_RX(EBUF_Rx), .MBUF_RX(MBUF_Rx), .FwdA(FwdA), .WbRx(WbRx), .FwdB(FwdB), .A(DBUF_A), .B(DBUF_B),
    .EBUF_OPCODE(EBUF_OPCODE), .MBUF_OPCODE(MBUF_OPCODE), .WbOPCODE(out_5));
  Adder #(.width(32)) adder_1 (.a(PC), .b(32'h1), .out(NPC));  // open: cin, cout
  Multiplexer #(.width(32), .disabled(0), .enable("false")) multiplexer_3 (
    .in0(NPC), .in1({32{1'b0}}), .out(multiplexer_3_out), .sel(FLUSH));
  RAM #(.addrWidth(24), .dataWidth(32)) ram_1 (
    .addr(bit_extender_1_out), .data(ram_1_data), .clk(CLK), .clr(in_1));  // open: sel, ld
  Multiplexer #(.width(32), .disabled(0), .enable("false")) multiplexer_4 (
    .in0(ram_1_data), .in1({32{1'b0}}), .out(multiplexer_4_out), .sel(FLUSH));
  Multiplexer #(.disabled(0), .enable("false")) multiplexer_5 (.in0(1'b1), .in1(1'b0), .out(EN), .sel(STALL));
  Multiplexer #(.width(32), .disabled(0), .enable("false")) multiplexer_6 (
    .in0(multiplexer_3_out), .in1(FBUF_PC), .out(multiplexer_6_out), .sel(STALL));
  Multiplexer #(.width(32), .disabled(0), .enable("false")) multiplexer_7 (
    .in0(multiplexer_4_out), .in1({out_4, DBUF_RX, DBUF_RY, FBUF_IR, DBUF_RZ}), .out(multiplexer_7_out),
    .sel(STALL));
  IF_IDRR_Buffer FBUF (
    .NPC(multiplexer_6_out), .MEM_PC(multiplexer_7_out), .WrEN(EN), .CLK(CLK), .RST(in_1), .FBUF_PC(FBUF_PC),
    .FBUF_IR({out_4, DBUF_RX, DBUF_RY, FBUF_IR, DBUF_RZ}));
  Multiplexer #(.width(32), .disabled(0), .enable("false")) multiplexer_8 (
    .in0(IROUT), .in1(WbPC), .out(INPUT), .sel(CALL));
  ID_Controller ID (
    .FBUF_IR({out_4, DBUF_RX, DBUF_RY, FBUF_IR, DBUF_RZ}), .FBUF_PC(FBUF_PC), .WbResult(WbResult),
    .Din(IROUT), .SR1(out_2), .SR2(out_3));
  and GOTO (GOTO_out, ~out_4[0], ~out_4[1], out_4[2], ~out_4[3]);  // AND_Gate
  and u_CALL (CALL_out, ~out_4[0], ~out_4[1], out_4[2], out_4[3]);  // AND_Gate
  and u_SKP (SKP, out_4[0], out_4[1], ~out_4[2], ~out_4[3]);  // AND_Gate
  and RET (RET_out, out_4[0], ~out_4[1], out_4[2], out_4[3]);  // AND_Gate
  and u_LEA (LEA_out, out_4[0], ~out_4[1], out_4[2], ~out_4[3]);  // AND_Gate
  or or_1 (FLUSH, Cond, SKIP);
  or or_2 (Cond, GOTO_out, CALL_out, RET_out);
  or or_3 (or_3_out, GOTO_out, LEA_out);
  Dual_Ported_Register_File dual_ported_register_file_1 (
    .CLK(CLK), .WrREGNO(WbRx), .RdREGNO1(out_2), .RdREGNO2(out_3), .INPUT(INPUT), .OUT1(DBUF_A),
    .OUT2(DBUF_B), .WrEN(WtReg));
  Staller Staller (.EBUF_OPCODE(EBUF_OPCODE), .SR1(out_2), .SR2(out_3), .EBUF_Rx(EBUF_Rx), .STALL(STALL));
  Multiplexer #(.width(32), .disabled(0), .enable("false")) multiplexer_9 (
    .in0(Imm), .in1(PDaddr24), .out(Offset), .sel(or_3_out));
  assign Imm = {{12{FBUF_IR[19]}}, {FBUF_IR, DBUF_RZ}};  // Bit_Extender bit_extender_2
  assign PDaddr24 = {{8{DBUF_RY[3]}}, {DBUF_RY, FBUF_IR, DBUF_RZ}};  // Bit_Extender bit_extender_3
  not not_2 (not_2_out, comparator_1_eq);
  Comparator #(.width(32), .mode("unsigned")) comparator_1 (
    .a(FwdA), .b(FwdB), .gt(comparator_1_gt), .eq(comparator_1_eq));  // open: lt
  not not_3 (not_3_out, comparator_1_gt);
  Multiplexer #(.select(4), .width(32), .disabled(0), .enable("false")) multiplexer_10 (
    .in4(PDaddr24), .in12(FwdB), .in13(FwdB), .out(BrPC), .sel(out_4));  // open: in0, in1, in2, in3, in5, in6, in7, in8, in9, in10, in11, in14, in15
  Multiplexer #(.disabled(0), .enable("false")) multiplexer_11 (
    .in0(not_2_out), .in1(not_3_out), .out(multiplexer_11_out), .sel(DBUF_RX[0]));
  and and_2 (SKIP, multiplexer_11_out, SKP);
  and ADDI (ADDI_out, EBUF_OPCODE[0], ~EBUF_OPCODE[1], ~EBUF_OPCODE[2], ~EBUF_OPCODE[3]);  // AND_Gate
  and LEA_2 (LEA, EBUF_OPCODE[0], ~EBUF_OPCODE[1], EBUF_OPCODE[2], ~EBUF_OPCODE[3]);  // AND_Gate
  and LW (LW_out, ~EBUF_OPCODE[0], ~EBUF_OPCODE[1], ~EBUF_OPCODE[2], EBUF_OPCODE[3]);  // AND_Gate
  and SW (SW_out, EBUF_OPCODE[0], ~EBUF_OPCODE[1], ~EBUF_OPCODE[2], EBUF_OPCODE[3]);  // AND_Gate
  or or_4 (E_I_type, ADDI_out, LEA, LW_out, SW_out);
  Multiplexer #(.width(32), .disabled(0), .enable("false")) multiplexer_12 (
    .in0(EBUF_B), .in1(E_Imm), .out(multiplexer_12_out), .sel(E_I_type));
  Multiplexer #(.width(32), .disabled(0), .enable("false")) multiplexer_13 (
    .in0(FwdA), .in1({32{1'b0}}), .out(multiplexer_13_out), .sel(or_5_out));
  Multiplexer #(.width(4), .disabled(0), .enable("false")) multiplexer_14 (
    .in0(DBUF_RX), .in1(4'b0000), .out(multiplexer_14_out), .sel(or_5_out));
  Multiplexer #(.width(32), .disabled(0), .enable("false")) multiplexer_15 (
    .in0(FwdB), .in1({32{1'b0}}), .out(multiplexer_15_out), .sel(or_5_out));
  Multiplexer #(.width(4), .disabled(0), .enable("false")) multiplexer_16 (
    .in0(out_4), .in1(out_4), .out(multiplexer_16_out), .sel(or_5_out));
  Multiplexer #(.width(32), .disabled(0), .enable("false")) multiplexer_17 (
    .in0(Offset), .in1({32{1'b0}}), .out(multiplexer_17_out), .sel(or_5_out));
  Multiplexer #(.width(32), .disabled(0), .enable("false")) multiplexer_18 (
    .in0(FBUF_PC), .in1(FBUF_PC), .out(multiplexer_18_out), .sel(or_5_out));
  or or_5 (or_5_out, STALL, FLUSH);
  ALU alu_1 (.\output (B_ALUout), .OpCode(EBUF_OPCODE), .A(EBUF_A), .B(multiplexer_12_out));
  IDRR_EX_Buffer DBUF (
    .DBUF_A(multiplexer_13_out), .DBUF_Rx(multiplexer_14_out), .DBUF_B(multiplexer_15_out),
    .DBUF_OPCODE(multiplexer_16_out), .EBUF_A(EBUF_A), .EBUF_Rx(EBUF_Rx), .EBUF_B(EBUF_B),
    .EBUF_OPCODE(EBUF_OPCODE), .in_1(CLK), .in_2(in_1), .Imm(multiplexer_17_out), .Imm_2(E_Imm),
    .DBUF_PC(multiplexer_18_out), .EBUF_PC(EBUF_PC));
  Multiplexer #(.width(32), .disabled(0), .enable("false")) multiplexer_19 (
    .in0(B_ALUout), .in1(E_Imm), .out(multiplexer_19_out), .sel(LEA));
  EX_MEM_Buffer EBUF (
    .EBUF_RESULT(multiplexer_19_out), .EBUF_RxVal(EBUF_B), .EBUF_OPCODE(EBUF_OPCODE), .EBUF_RX(EBUF_Rx),
    .MAR(MAR), .Din(Din), .MBUF_OPCODE(MBUF_OPCODE), .MBUF_Rx(MBUF_Rx), .in_1(CLK), .in_2(in_1),
    .EBUF_PC(EBUF_PC), .MBUF_PC(MBUF_PC));
  RAM #(.addrWidth(24), .dataWidth(32), .bus("separate")) ram_2 (
    .addr(MAR[23:0]), .din(Din), .data(ram_2_data), .str(WtMem), .clk(CLK), .ld(LW_2_out), .clr(in_1));  // open: sel
  and LW_2 (LW_2_out, ~MBUF_OPCODE[0], ~MBUF_OPCODE[1], ~MBUF_OPCODE[2], MBUF_OPCODE[3]);  // AND_Gate
  and SW_2 (WtMem, MBUF_OPCODE[0], ~MBUF_OPCODE[1], ~MBUF_OPCODE[2], MBUF_OPCODE[3]);  // AND_Gate
  Multiplexer #(.width(32), .disabled(0), .enable("false")) multiplexer_20 (
    .in0(MAR), .in1(ram_2_data), .out(MBUF_RESULT), .sel(LW_2_out));
  Multiplexer #(.select(4), .disabled(0), .enable("false")) multiplexer_21 (
    .in0(1'b1), .in1(1'b1), .in2(1'b1), .in3(1'b0), .in4(1'b0), .in5(1'b1), .in6(1'b0), .in7(1'b0),
    .in8(1'b1), .in9(1'b0), .in11(1'b0), .in12(1'b1), .in13(1'b0), .in14(1'b0), .in15(1'b0), .out(WtReg),
    .sel(out_5));  // open: in10
  MEM_WB_Buffer MBUF (
    .MBUF_RESULT(MBUF_RESULT), .MBUF_Rx(MBUF_Rx), .MBUF_Opcode(MBUF_OPCODE), .MBUF_PC(MBUF_PC),
    .WbResult(WbResult), .WbRx(MBUF_wbrx), .WbOpcode(out_5), .WbPC(WbPC), .in_1(CLK), .in_2(in_1));
  Multiplexer #(.width(4), .disabled(0), .enable("false")) multiplexer_22 (
    .in0(MBUF_wbrx), .in1(4'b1111), .out(WbRx), .sel(CALL));
  and CALL_2 (CALL, ~out_5[0], ~out_5[1], out_5[2], out_5[3]);  // AND_Gate

  // Other names for the same wires on the sheet: FBUF_IR (some bits) = {out_4, DBUF_RX, DBUF_RY, DBUF_RZ};
  //   DBUF_OPCODE[3:0] = out_4; RST = in_1; SR1[3:0] = out_2; SR2[3:0] = out_3; WbOPCODE[3:0] = out_5
endmodule

module Dual_Ported_Register_File (
  input  CLK,
  input  WrEN,
  input  [3:0] WrREGNO,
  input  [3:0] RdREGNO1,
  input  [3:0] RdREGNO2,
  input  [31:0] INPUT,
  output [31:0] OUT1,
  output [31:0] OUT2
);

  wire En_a0, En_a1, En_a2, En_at, En_fp, En_k0, En_ra, En_s0, En_s1, En_s2, En_sp, En_t0, En_t1, En_t2,
       En_v0;
  wire [31:0] a0, a1, a2, at, fp, k0, ra, s0, s1, s2, sp, t0, t1, t2, v0, zero;

  Decoder #(.select(4), .disabled(0)) decoder_1 (
    .out1(En_at), .out2(En_v0), .out3(En_a0), .out4(En_a1), .out5(En_a2), .out6(En_t0), .out7(En_t1),
    .out8(En_t2), .out9(En_s0), .out10(En_s1), .out11(En_s2), .out12(En_k0), .out13(En_sp), .out14(En_fp),
    .out15(En_ra), .sel(WrREGNO), .en(WrEN));  // open: out0
  Register #(.width(32)) u_zero (.D(INPUT), .en(1'b0), .Q(zero), .clk(CLK));  // open: clr
  Register #(.width(32)) u_at (.D(INPUT), .en(En_at), .Q(at), .clk(CLK));  // open: clr
  Register #(.width(32)) u_v0 (.D(INPUT), .en(En_v0), .Q(v0), .clk(CLK));  // open: clr
  Register #(.width(32)) u_a0 (.D(INPUT), .en(En_a0), .Q(a0), .clk(CLK));  // open: clr
  Register #(.width(32)) u_a1 (.D(INPUT), .en(En_a1), .Q(a1), .clk(CLK));  // open: clr
  Register #(.width(32)) u_a2 (.D(INPUT), .en(En_a2), .Q(a2), .clk(CLK));  // open: clr
  Register #(.width(32)) u_t0 (.D(INPUT), .en(En_t0), .Q(t0), .clk(CLK));  // open: clr
  Register #(.width(32)) u_t1 (.D(INPUT), .en(En_t1), .Q(t1), .clk(CLK));  // open: clr
  Multiplexer #(.select(4), .width(32), .disabled(0), .enable("false")) multiplexer_1 (
    .in0(zero), .in1(at), .in2(v0), .in3(a0), .in4(a1), .in5(a2), .in6(t0), .in7(t1), .in8(t2), .in9(s0),
    .in10(s1), .in11(s2), .in12(k0), .in13(sp), .in14(fp), .in15(ra), .out(OUT2), .sel(RdREGNO2));
  Register #(.width(32)) u_t2 (.D(INPUT), .en(En_t2), .Q(t2), .clk(CLK));  // open: clr
  Register #(.width(32)) u_s0 (.D(INPUT), .en(En_s0), .Q(s0), .clk(CLK));  // open: clr
  Register #(.width(32)) u_s1 (.D(INPUT), .en(En_s1), .Q(s1), .clk(CLK));  // open: clr
  Register #(.width(32)) u_s2 (.D(INPUT), .en(En_s2), .Q(s2), .clk(CLK));  // open: clr
  Register #(.width(32)) u_k0 (.D(INPUT), .en(En_k0), .Q(k0), .clk(CLK));  // open: clr
  Register #(.width(32)) u_sp (.D(INPUT), .en(En_sp), .Q(sp), .clk(CLK));  // open: clr
  Register #(.width(32)) u_fp (.D(INPUT), .en(En_fp), .Q(fp), .clk(CLK));  // open: clr
  Register #(.width(32)) u_ra (.D(INPUT), .en(En_ra), .Q(ra), .clk(CLK));  // open: clr
  Multiplexer #(.select(4), .width(32), .disabled(0), .enable("false")) multiplexer_2 (
    .in0(zero), .in1(at), .in2(v0), .in3(a0), .in4(a1), .in5(a2), .in6(t0), .in7(t1), .in8(t2), .in9(s0),
    .in10(s1), .in11(s2), .in12(k0), .in13(sp), .in14(fp), .in15(ra), .out(OUT1), .sel(RdREGNO1));

  // Notes on the sheet:
  //   MODIFY AT YOUR OWN RISK
endmodule

module IF_IDRR_Buffer (
  input  [31:0] NPC,
  input  [31:0] MEM_PC,
  input  CLK,
  input  RST,
  input  WrEN,
  output [31:0] FBUF_PC,
  output [31:0] FBUF_IR
);

  Register #(.width(32)) register_1 (.D(NPC), .en(WrEN), .Q(FBUF_PC), .clk(CLK), .clr(RST));
  Register #(.width(32)) register_2 (.D(MEM_PC), .en(WrEN), .Q(FBUF_IR), .clk(CLK), .clr(RST));
endmodule

module IDRR_EX_Buffer (
  input  in_1,
  input  in_2,
  input  [3:0] DBUF_OPCODE,
  input  [3:0] DBUF_Rx,
  input  [31:0] DBUF_A,
  input  [31:0] DBUF_B,
  input  [31:0] Imm,
  input  [31:0] DBUF_PC,
  output [3:0] EBUF_OPCODE,
  output [3:0] EBUF_Rx,
  output [31:0] EBUF_A,
  output [31:0] EBUF_B,
  output [31:0] Imm_2,
  output [31:0] EBUF_PC
);

  Register #(.width(4)) OPCODE (.D(DBUF_OPCODE), .Q(EBUF_OPCODE), .clk(in_1), .clr(in_2));  // open: en
  Register #(.width(4)) u_Imm (.D(DBUF_Rx), .Q(EBUF_Rx), .clk(in_1), .clr(in_2));  // open: en
  Register #(.width(32)) u_DBUF_A (.D(DBUF_A), .Q(EBUF_A), .clk(in_1), .clr(in_2));  // open: en
  Register #(.width(32)) u_DBUF_B (.D(DBUF_B), .Q(EBUF_B), .clk(in_1), .clr(in_2));  // open: en
  Register #(.width(32)) u_Imm_2 (.D(Imm), .Q(Imm_2), .clk(in_1), .clr(in_2));  // open: en
  Register #(.width(32)) PC (.D(DBUF_PC), .Q(EBUF_PC), .clk(in_1), .clr(in_2));  // open: en

  // Other names for the same wires on the sheet: CLK = in_1; RST = in_2
endmodule

module EX_MEM_Buffer (
  input  in_1,
  input  in_2,
  input  [31:0] EBUF_RESULT,
  input  [31:0] EBUF_RxVal,
  input  [3:0] EBUF_OPCODE,
  input  [3:0] EBUF_RX,
  input  [31:0] EBUF_PC,
  output [31:0] MAR,
  output [31:0] Din,
  output [3:0] MBUF_OPCODE,
  output [3:0] MBUF_Rx,
  output [31:0] MBUF_PC
);

  Register #(.width(32)) u_MAR (.D(EBUF_RESULT), .Q(MAR), .clk(in_1), .clr(in_2));  // open: en
  Register #(.width(32)) RxVal (.D(EBUF_RxVal), .Q(Din), .clk(in_1), .clr(in_2));  // open: en
  Register #(.width(4)) OPCODE (.D(EBUF_OPCODE), .Q(MBUF_OPCODE), .clk(in_1), .clr(in_2));  // open: en
  Register #(.width(4)) Rx (.D(EBUF_RX), .Q(MBUF_Rx), .clk(in_1), .clr(in_2));  // open: en
  Register #(.width(32)) PC (.D(EBUF_PC), .Q(MBUF_PC), .clk(in_1), .clr(in_2));  // open: en

  // Other names for the same wires on the sheet: CLK = in_1; RST = in_2
endmodule

module MEM_WB_Buffer (
  input  in_1,
  input  in_2,
  input  [31:0] MBUF_RESULT,
  input  [3:0] MBUF_Rx,
  input  [3:0] MBUF_Opcode,
  input  [31:0] MBUF_PC,
  output [31:0] WbResult,
  output [3:0] WbRx,
  output [3:0] WbOpcode,
  output [31:0] WbPC
);

  wire EN;

  Register #(.width(32)) DBUF_A (.D(MBUF_RESULT), .Q(WbResult), .clk(in_1), .clr(in_2));  // open: en
  Register #(.width(4)) Imm (.D(MBUF_Rx), .Q(WbRx), .clk(in_1), .clr(in_2));  // open: en
  Register #(.width(4)) Imm_2 (.D(MBUF_Opcode), .Q(WbOpcode), .clk(in_1), .clr(in_2));  // open: en
  Register #(.width(32)) DBUF_A_2 (.D(MBUF_PC), .en(EN), .Q(WbPC), .clk(in_1), .clr(in_2));

  // Other names for the same wires on the sheet: CLK = in_1; RST = in_2
endmodule

module Forwarding_Unit (
  input  [3:0] SR1,
  input  [3:0] SR2,
  input  [31:0] EBUF_RESULT,
  input  [31:0] MBUF_RESULT,
  input  [31:0] WbResult,
  input  [3:0] EBUF_RX,
  input  [3:0] MBUF_RX,
  input  [3:0] WbRx,
  input  [3:0] EBUF_OPCODE,
  input  [3:0] MBUF_OPCODE,
  input  [3:0] WbOPCODE,
  input  [31:0] A,
  input  [31:0] B,
  output [31:0] FwdA,
  output [31:0] FwdB
);

  wire comparator_1_eq, comparator_2_eq, comparator_3_eq, comparator_4_eq, comparator_5_eq, comparator_6_eq,
       EWt, FwdE1, FwdE2, FwdM1, FwdM2, FwdW1, FwdW2, MWt, WWt;
  wire [31:0] multiplexer_1_out, multiplexer_2_out, multiplexer_3_out, multiplexer_4_out;

  Multiplexer #(.width(32), .disabled(0), .enable("false")) multiplexer_1 (
    .in0(A), .in1(WbResult), .out(multiplexer_1_out), .sel(FwdW1));
  Multiplexer #(.width(32), .disabled(0), .enable("false")) multiplexer_2 (
    .in0(B), .in1(WbResult), .out(multiplexer_2_out), .sel(FwdW2));
  Multiplexer #(.width(32), .disabled(0), .enable("false")) multiplexer_3 (
    .in0(multiplexer_1_out), .in1(MBUF_RESULT), .out(multiplexer_3_out), .sel(FwdM1));
  Multiplexer #(.width(32), .disabled(0), .enable("false")) multiplexer_4 (
    .in0(multiplexer_2_out), .in1(MBUF_RESULT), .out(multiplexer_4_out), .sel(FwdM2));
  Comparator #(.width(4), .mode("unsigned")) comparator_1 (.a(SR2), .b(EBUF_RX), .eq(comparator_1_eq));  // open: gt, lt
  Comparator #(.width(4), .mode("unsigned")) comparator_2 (.a(SR1), .b(EBUF_RX), .eq(comparator_2_eq));  // open: gt, lt
  Comparator #(.width(4), .mode("unsigned")) comparator_3 (.a(SR2), .b(MBUF_RX), .eq(comparator_3_eq));  // open: gt, lt
  Comparator #(.width(4), .mode("unsigned")) comparator_4 (.a(SR1), .b(MBUF_RX), .eq(comparator_4_eq));  // open: gt, lt
  Comparator #(.width(4), .mode("unsigned")) comparator_5 (.a(SR2), .b(WbRx), .eq(comparator_5_eq));  // open: gt, lt
  Comparator #(.width(4), .mode("unsigned")) comparator_6 (.a(SR1), .b(WbRx), .eq(comparator_6_eq));  // open: gt, lt
  Multiplexer #(.width(32), .disabled(0), .enable("false")) multiplexer_5 (
    .in0(multiplexer_3_out), .in1(EBUF_RESULT), .out(FwdA), .sel(FwdE1));
  Multiplexer #(.width(32), .disabled(0), .enable("false")) multiplexer_6 (
    .in0(multiplexer_4_out), .in1(EBUF_RESULT), .out(FwdB), .sel(FwdE2));
  and and_1 (FwdE2, comparator_1_eq, EWt);
  and and_2 (FwdE1, comparator_2_eq, EWt);
  and and_3 (FwdM2, comparator_3_eq, MWt);
  and and_4 (FwdM1, comparator_4_eq, MWt);
  and and_5 (FwdW2, comparator_5_eq, WWt);
  and and_6 (FwdW1, comparator_6_eq, WWt);
  Multiplexer #(.select(4), .disabled(0), .enable("false")) multiplexer_7 (
    .in0(1'b1), .in1(1'b1), .in2(1'b1), .in3(1'b0), .in4(1'b0), .in5(1'b1), .in6(1'b1), .in7(1'b0),
    .in8(1'b0), .in9(1'b0), .in10(1'b0), .in11(1'b0), .in12(1'b0), .in13(1'b0), .in14(1'b0), .in15(1'b0),
    .out(EWt), .sel(EBUF_OPCODE));
  Multiplexer #(.select(4), .disabled(0), .enable("false")) multiplexer_8 (
    .in0(1'b1), .in1(1'b1), .in2(1'b1), .in3(1'b0), .in4(1'b0), .in5(1'b1), .in6(1'b1), .in7(1'b0),
    .in8(1'b0), .in9(1'b0), .in10(1'b0), .in11(1'b0), .in12(1'b0), .in13(1'b0), .in14(1'b0), .in15(1'b0),
    .out(MWt), .sel(MBUF_OPCODE));
  Multiplexer #(.select(4), .disabled(0), .enable("false")) multiplexer_9 (
    .in0(1'b1), .in1(1'b1), .in2(1'b1), .in3(1'b0), .in4(1'b0), .in5(1'b1), .in6(1'b1), .in7(1'b0),
    .in8(1'b0), .in9(1'b0), .in10(1'b0), .in11(1'b0), .in12(1'b0), .in13(1'b0), .in14(1'b0), .in15(1'b0),
    .out(WWt), .sel(WbOPCODE));
endmodule

module ALU (
  input  [3:0] OpCode,
  input  [31:0] A,
  input  [31:0] B,
  output [31:0] \output 
);

  wire [31:0] adder_1_out, nand_1_out;

  Adder #(.width(32)) adder_1 (.a(A), .b(B), .out(adder_1_out));  // open: cin, cout
  Multiplexer #(.select(2), .width(32), .disabled(0), .enable("false")) multiplexer_1 (
    .in0(adder_1_out), .in1(adder_1_out), .in2(nand_1_out), .in3({32{1'b0}}), .out(\output ),
    .sel(OpCode[1:0]));
  assign nand_1_out = ~(A & B);  // NAND_Gate nand_1, 32 bits wide
endmodule

module ID_Controller (
  input  [31:0] FBUF_IR,
  input  [31:0] FBUF_PC,
  input  [31:0] WbResult,
  output [31:0] Din,
  output [3:0] SR1,
  output [3:0] SR2
);

  wire CALL_out, Dout2, RET_out, SW_out;
  wire [3:0] multiplexer_1_out;

  Multiplexer #(.width(4), .disabled(0), .enable("false")) multiplexer_1 (
    .in0(FBUF_IR[3:0]), .in1(FBUF_IR[27:24]), .out(multiplexer_1_out), .sel(Dout2));
  Multiplexer #(.width(4), .disabled(0), .enable("false")) multiplexer_2 (
    .in0(multiplexer_1_out), .in1(4'b1111), .out(SR2), .sel(RET_out));
  and SW (SW_out, FBUF_IR[28], ~FBUF_IR[29], ~FBUF_IR[30], FBUF_IR[31]);  // AND_Gate
  and CALL (CALL_out, ~FBUF_IR[28], ~FBUF_IR[29], FBUF_IR[30], FBUF_IR[31]);  // AND_Gate
  and RET (RET_out, FBUF_IR[28], ~FBUF_IR[29], FBUF_IR[30], FBUF_IR[31]);  // AND_Gate
  or or_1 (Dout2, SW_out, CALL_out);

  assign Din = WbResult;
  assign SR1 = FBUF_IR[23:20];

  // Other names for the same wires on the sheet: DBUF_RZ[3:0] = FBUF_IR[3:0]; DBUF_RY[3:0] = FBUF_IR[23:20];
  //   DBUF_RX[3:0] = FBUF_IR[27:24]; DBUF_OPCODE[3:0] = FBUF_IR[31:28]
endmodule

module Staller (
  input  [3:0] EBUF_OPCODE,
  input  [3:0] SR1,
  input  [3:0] SR2,
  input  [3:0] EBUF_Rx,
  output STALL
);

  wire ADDI_out, comparator_1_eq, comparator_2_eq, LW_out, NAND_out, or_1_out, or_2_out, SW_out;

  and ADDI (ADDI_out, EBUF_OPCODE[0], ~EBUF_OPCODE[1], ~EBUF_OPCODE[2], ~EBUF_OPCODE[3]);  // AND_Gate
  and LW (LW_out, ~EBUF_OPCODE[0], ~EBUF_OPCODE[1], ~EBUF_OPCODE[2], EBUF_OPCODE[3]);  // AND_Gate
  and SW (SW_out, EBUF_OPCODE[0], ~EBUF_OPCODE[1], ~EBUF_OPCODE[2], EBUF_OPCODE[3]);  // AND_Gate
  and NAND (NAND_out, ~EBUF_OPCODE[0], EBUF_OPCODE[1], ~EBUF_OPCODE[2], ~EBUF_OPCODE[3]);  // AND_Gate
  Comparator #(.width(4), .mode("unsigned")) comparator_1 (.a(SR1), .b(EBUF_Rx), .eq(comparator_1_eq));  // open: gt, lt
  Comparator #(.width(4), .mode("unsigned")) comparator_2 (.a(SR2), .b(EBUF_Rx), .eq(comparator_2_eq));  // open: gt, lt
  buf or_1 (or_1_out, LW_out);  // OR_Gate
  or or_2 (or_2_out, comparator_1_eq, comparator_2_eq);
  and and_1 (STALL, or_1_out, or_2_out);
endmodule
